# Fritzing sketch Fritz_final (saved by Fritzing 0.9.3b)
breadboards: 1

parts:
  Composant1 = Arduino Uno (Rev3)
  R1 = Temperature Sensor (Thermistor) [thermistor_type=NTC package=THT]
  R2 = Temperature Sensor (Thermistor) [thermistor_type=NTC package=THT]
  R3 = Resistor [tolerance=±5% resistance=10k package="0603 [SMD]"]
  R4 = Resistor [tolerance=±5% resistance=10k package="0603 [SMD]"]
  RHT1 = Humidity and Temperature Sensor RHT03
  J1 = Peltier Element
  M1 = DC Motor
  VCC1 = Battery
  Q1 = PNP-Transistor [package="TO92 [THT]"]

nets:
  N1: Composant1.A0, R2.pin_1, R4.Pin_0
  N2: Composant1.A1, R1.pin_1, R3.Pin_0
  N3: Composant1.D2, RHT1.Data-signal
  N4: Composant1.D3_PWM, Q1.B
  5V: Composant1.5V, R3.Pin_1, R4.Pin_1, RHT1.Vcc
  N5: Composant1.GND, R1.pin_0, R2.pin_0, RHT1.GND_2
  N6: J1.pin1, Q1.E
  N7: J1.pin2, M1.pin_1
  N8: M1.pin_2, VCC1.-
  N9: VCC1.+, Q1.C
