# Fritzing sketch Schéma électrique (saved by Fritzing 0.9.3b)
breadboards: 1

parts:
  Arduino = Arduino Uno (Rev3)
  R1 = Temperature Sensor (Thermistor) [thermistor_type=NTC package=THT]
  R2 = Temperature Sensor (Thermistor) [thermistor_type=NTC package=THT]
  R3 = Resistor [tolerance=±5% resistance=10k package="0603 [SMD]"]
  R4 = Resistor [tolerance=±5% resistance=10k package="0603 [SMD]"]
  RHT1 = Humidity and Temperature Sensor RHT03
  Peltier = Peltier Element
  Ventilateur = DC Motor
  VCC1 = Battery block 9V
  Q2 = NPN-Transistor [package="TO92 [THT]"]

nets:
  N1: Arduino.A0, R2.pin_1, R4.Pin_0
  N2: Arduino.A1, R1.pin_1, R3.Pin_0
  N3: Arduino.D2, RHT1.Data-signal
  N4: Arduino.D3_PWM, Q2.B
  N5: Peltier.pin1, Q2.E
  N6: Peltier.pin2, Ventilateur.pin_1
  N7: Ventilateur.pin_2, VCC1.-
  N8: VCC1.+, Q2.C
