# Fritzing sketch old_fritz (saved by Fritzing 0.9.3b)
breadboards: 2

parts:
  Composant1 = Arduino Uno (Rev3)
  R1 = Resistor [tolerance=±5% resistance=220 package=THT]
  U1 = LM 358 Dual Op-Amp [package="DIP8 [THT]"]
  D1 = Rectifier Diode [part_number=1N4001 package="300 mil [THT]"]
  R2 = Resistor [tolerance=±5% resistance=220 package=THT]
  D2 = Rectifier Diode [part_number=1N4001 package="300 mil [THT]"]
  Q1 = MOSFET-NCHANNEL [package=to-92]
  Q2 = MOSFET-NCHANNEL [package=to-92]
  Power_plug1 = Power plug
  M1 = DC Motor
  J1 = Peltier Element

nets:
  N1: Composant1.A0, U1.connector6
  N2: Composant1.A1, U1.connector0
  N3: Composant1.D8, Q1.S
  N4: Composant1.D7, Q2.S
  N5: Composant1.5V, R1.Pin_0, U1.connector2, U1.connector4, U1.connector7, R2.Pin_0
  N6: R1.Pin_1, U1.connector1, D1.cathode
  N7: U1.connector3, D1.anode, D2.anode
  N8: U1.connector5, R2.Pin_1, D2.cathode
  N9: Q1.D, J1.pin2
  N10: Q1.G, Q2.G, Power_plug1.VCC
  N11: Q2.D, M1.pin_2
  N12: Power_plug1.GND, M1.pin_1, J1.pin1
